# Fritzing sketch schematic (saved by Fritzing 0.9.3b)
perfboards: 1

parts:
  U2 = LCD-16X2 [package=lcd-16x2_noholes]
  R1 = Resistor [tolerance=±5% resistance=220 package=THT]  # not connected
  R2 = TRIMPOT [package=3386u]
  J1 = female pin header, 16 pins [form="♀ (female)"]
  J2 = male pin header, 5 pins [form="♂ (male)"]  # not connected
  J3 = male pin header, 5 pins [form="♂ (male)"]  # not connected
  J4 = male pin header, 2 pins [form="♂ (male)"]  # not connected
  J5 = male pin header, 2 pins [form="♂ (male)"]

nets:
  N1: U2.VSS, J1.pin16
  N2: U2.VDD, J1.pin15
  N3: U2.VO, J1.pin14
  N4: U2.RS, J1.pin13
  N5: U2.R_W, J1.pin12
  N6: U2.E, J1.pin11
  N7: U2.DB0, J1.pin10
  N8: U2.DB1, J1.pin9
  N9: U2.DB2, J1.pin8
  N10: U2.DB3, J1.pin7
  N11: U2.DB4, J1.pin6
  N12: U2.DB5, J1.pin5
  N13: U2.DB6, J1.pin4
  N14: U2.DB7, J1.pin3
  N15: U2.A, J1.pin2
  N16: U2.K, J1.pin1
  N17: R2.CCW, J5.pin2

notes:
  Vdd
  RS
  EN
  LCD2
  LCD3
  LCD4
  LCD1
  GND
  1
  14
  15
  R/W
